// Logisim project datapath.circ as structural Verilog: 8 circuits, main circuit PC
module main (
  input  reset
);

  wire and_1_out, clock_1_out, control_1_branch_absolute, control_1_branch_relative, control_1_immediate_rt,
       control_1_memread, control_1_memwrite, control_1_regwrite, control_1_save_pc,
       control_1_storefromregister, is_zero_8_1_out_2, not_1_out;
  wire [1:0] control_1_alu_op;
  wire [2:0] control_1_rd, control_1_rs, control_1_rt;
  wire [7:0] alu_1_r, bit_extender_1_out, control_1_branch_value, multiplexer_1_out, multiplexer_2_out,
       multiplexer_3_out, multiplexer_4_out, pc_1_pc, ram_1_data, registerfile_1_ap, registerfile_1_s,
       registerfile_1_t;
  wire [8:0] rom_1_data;

  is_zero_8 is_zero_8_1 (.in_1(ram_1_data), .out_2(is_zero_8_1_out_2));
  not not_1 (not_1_out, is_zero_8_1_out_2);
  and and_1 (and_1_out, not_1_out, control_1_memread, control_1_branch_relative);
  PC pc_1 (
    .Branch_relative(and_1_out), .Branch_absolute(control_1_branch_absolute),
    .Branch_offset(control_1_branch_value), .C(clock_1_out), .r(reset), .PC(pc_1_pc));
  Clock clock_1 (.out(clock_1_out));
  ROM #(.dataWidth(9)) rom_1 (.addr(pc_1_pc), .data(rom_1_data));  // open: sel
  Control control_1 (
    .Instruction(rom_1_data), .rs(control_1_rs), .rt(control_1_rt), .immediate_rt(control_1_immediate_rt),
    .rd(control_1_rd), .regwrite(control_1_regwrite), .ALU_OP(control_1_alu_op), .memread(control_1_memread),
    .memwrite(control_1_memwrite), .branch_value(control_1_branch_value),
    .branch_relative(control_1_branch_relative), .branch_absolute(control_1_branch_absolute),
    .save_PC(control_1_save_pc), .storeFromRegister(control_1_storefromregister));
  RegisterFile registerfile_1 (
    .rs(control_1_rs), .rt(control_1_rt), .rd(control_1_rd), .Data(multiplexer_1_out),
    .write(control_1_regwrite), .reset(reset), .C(clock_1_out), .S(registerfile_1_s), .T(registerfile_1_t),
    .AP(registerfile_1_ap));
  assign bit_extender_1_out = {{5{control_1_rt[2]}}, control_1_rt};  // Bit_Extender bit_extender_1
  Multiplexer #(.width(8), .enable("false")) multiplexer_1 (
    .in0(alu_1_r), .in1(ram_1_data), .out(multiplexer_1_out), .sel(control_1_memread));
  ALU alu_1 (.OP_code(control_1_alu_op), .A(registerfile_1_s), .B(multiplexer_2_out), .R(alu_1_r));
  Multiplexer #(.width(8), .enable("false")) multiplexer_2 (
    .in0(registerfile_1_t), .in1(bit_extender_1_out), .out(multiplexer_2_out), .sel(control_1_immediate_rt));
  Multiplexer #(.width(8), .enable("false")) multiplexer_3 (
    .in0(alu_1_r), .in1(pc_1_pc), .out(multiplexer_3_out), .sel(control_1_save_pc));
  Multiplexer #(.width(8), .enable("false")) multiplexer_4 (
    .in0(multiplexer_3_out), .in1(registerfile_1_s), .out(multiplexer_4_out),
    .sel(control_1_storefromregister));
  RAM #(.bus("separate")) ram_1 (
    .addr(registerfile_1_ap), .din(multiplexer_4_out), .data(ram_1_data), .str(control_1_memwrite),
    .clk(clock_1_out), .ld(control_1_memread), .clr(reset));  // open: sel

  // Notes on the sheet:
  //   contents of rom_1 (hex, n*v repeats v):
  //   9 d 39 d 39 3a 3a c 39 14 39 14a 39 85
endmodule

module PC (
  input  Branch_relative,
  input  Branch_absolute,
  input  [7:0] Branch_offset,
  input  C,
  input  r,
  output [7:0] PC
);

  wire [7:0] adder_1_out, adder_2_out, multiplexer_1_out, multiplexer_2_out;

  Adder adder_1 (.a(8'h1), .b(Branch_offset), .out(adder_1_out));  // open: cin, cout
  Multiplexer #(.width(8), .enable("false")) multiplexer_1 (
    .in0(8'h1), .in1(adder_1_out), .out(multiplexer_1_out), .sel(Branch_relative));
  Adder adder_2 (.a(multiplexer_1_out), .b(PC), .out(adder_2_out));  // open: cin, cout
  Multiplexer #(.width(8), .enable("false")) multiplexer_2 (
    .in0(adder_2_out), .in1(Branch_offset), .out(multiplexer_2_out), .sel(Branch_absolute));
  Register #(.trigger("falling")) register_1 (.D(multiplexer_2_out), .Q(PC), .clk(C), .clr(r));  // open: en
endmodule

module ALU (
  input  [1:0] OP_code,
  input  [7:0] A,
  input  [7:0] B,
  output [7:0] R
);

  wire [7:0] adder_1_out, negator_1_out, or_1_out, subtractor_1_out;

  assign or_1_out = A | B;  // OR_Gate or_1, 8 bits wide
  Adder adder_1 (.a(A), .b(B), .out(adder_1_out));  // open: cin, cout
  Subtractor subtractor_1 (.a(A), .b(B), .out(subtractor_1_out));  // open: bin, bout
  Negator negator_1 (.in(A), .out(negator_1_out));
  Multiplexer #(.select(2), .width(8), .enable("false")) multiplexer_1 (
    .in0(or_1_out), .in1(adder_1_out), .in2(subtractor_1_out), .in3(negator_1_out), .out(R), .sel(OP_code));
endmodule

module RegisterFile (
  input  [2:0] rs,
  input  [2:0] rt,
  input  [2:0] rd,
  input  [7:0] Data,
  input  write,
  input  reset,
  input  C,
  output [7:0] S,
  output [7:0] T,
  output [7:0] AP
);

  wire and_1_out, and_2_out, and_3_out, and_4_out, and_5_out, and_6_out, and_7_out, decoder_1_out0,
       decoder_1_out1, decoder_1_out2, decoder_1_out3, decoder_1_out4, decoder_1_out5, decoder_1_out6,
       decoder_1_out7;
  wire [7:0] register_1_q, register_2_q, register_3_q, register_4_q, register_5_q, register_6_q;

  Decoder #(.select(3), .enable("false")) decoder_1 (
    .out0(decoder_1_out0), .out1(decoder_1_out1), .out2(decoder_1_out2), .out3(decoder_1_out3),
    .out4(decoder_1_out4), .out5(decoder_1_out5), .out6(decoder_1_out6), .out7(decoder_1_out7), .sel(rd));
  Pull_Resistor pull_resistor_1 (.node(decoder_1_out0));
  and and_1 (and_1_out, decoder_1_out2, write);
  and and_2 (and_2_out, decoder_1_out3, write);
  Register #(.trigger("falling")) register_1 (.D(Data), .en(and_3_out), .Q(register_1_q), .clk(C), .clr(reset));
  and and_3 (and_3_out, decoder_1_out1, write);
  Register #(.trigger("falling")) register_2 (.D(Data), .en(and_1_out), .Q(register_2_q), .clk(C), .clr(reset));
  Register #(.trigger("falling")) register_3 (.D(Data), .en(and_2_out), .Q(register_3_q), .clk(C), .clr(reset));
  and and_4 (and_4_out, decoder_1_out4, write);
  and and_5 (and_5_out, decoder_1_out5, write);
  and and_6 (and_6_out, decoder_1_out6, write);
  and and_7 (and_7_out, decoder_1_out7, write);
  Register #(.trigger("falling")) register_4 (.D(Data), .en(and_4_out), .Q(register_4_q), .clk(C), .clr(reset));
  Register #(.trigger("falling")) register_5 (.D(Data), .en(and_5_out), .Q(register_5_q), .clk(C), .clr(reset));
  Register #(.trigger("falling")) register_6 (.D(Data), .en(and_6_out), .Q(register_6_q), .clk(C), .clr(reset));
  Register #(.trigger("falling")) register_7 (.D(Data), .en(and_7_out), .Q(AP), .clk(C), .clr(reset));
  Multiplexer #(.select(3), .width(8), .enable("false")) multiplexer_1 (
    .in0({8{1'b0}}), .in1(register_1_q), .in2(register_2_q), .in3(register_3_q), .in4(register_4_q),
    .in5(register_5_q), .in6(register_6_q), .in7(AP), .out(S), .sel(rs));
  Multiplexer #(.select(3), .width(8), .enable("false")) multiplexer_2 (
    .in0({8{1'b0}}), .in1(register_1_q), .in2(register_2_q), .in3(register_3_q), .in4(register_4_q),
    .in5(register_5_q), .in6(register_6_q), .in7(AP), .out(T), .sel(rt));
endmodule

module Control (
  input  [8:0] Instruction,
  output [2:0] rs,
  output [2:0] rt,
  output immediate_rt,
  output [2:0] rd,
  output regwrite,
  output [1:0] ALU_OP,
  output memread,
  output memwrite,
  output [7:0] branch_value,
  output branch_relative,
  output branch_absolute,
  output save_PC,
  output storeFromRegister
);

  wire and_1_out, and_2_out, and_4_out, and_6_out, and_7_out, and_8_out, is_full_1_out_2, is_zero_1_out_2,
       is_zero_2_out_2, not_1_out, not_2_out, not_3_out, not_4_out, not_5_out, not_6_out, not_7_out,
       not_8_out, not_9_out, or_1_out, xor_1_out;
  wire [2:0] multiplexer_1_out;

  is_zero is_zero_1 (.in_1(Instruction[2:0]), .out_2(is_zero_1_out_2));
  is_zero is_zero_2 (.in_1(Instruction[8:6]), .out_2(is_zero_2_out_2));
  xor xor_1 (xor_1_out, Instruction[1], Instruction[0]);
  is_full is_full_1 (.in_1(Instruction[8:6]), .out_2(is_full_1_out_2));
  and and_1 (and_1_out, is_full_1_out_2, is_zero_1_out_2);
  Multiplexer #(.width(3), .enable("false")) multiplexer_1 (
    .in0(Instruction[2:0]), .in1(3'b000), .out(multiplexer_1_out), .sel(and_1_out));
  and and_2 (and_2_out, Instruction[2], is_zero_2_out_2);
  not not_1 (not_1_out, Instruction[8]);
  not not_2 (not_2_out, Instruction[7]);
  and and_3 (branch_relative, not_1_out, not_2_out, Instruction[6]);
  not not_3 (not_3_out, Instruction[8]);
  and and_4 (and_4_out, not_3_out, Instruction[7], not_4_out);
  not not_4 (not_4_out, Instruction[6]);
  not not_5 (not_5_out, Instruction[8]);
  and and_5 (save_PC, not_5_out, Instruction[7], Instruction[6]);
  and and_6 (and_6_out, is_zero_2_out_2, is_zero_1_out_2, xor_1_out);
  Multiplexer #(.width(3), .enable("false")) multiplexer_2 (
    .in0(Instruction[5:3]), .in1(3'b000), .out(rs), .sel(and_6_out));
  Multiplexer #(.width(3), .enable("false")) multiplexer_3 (
    .in0(multiplexer_1_out), .in1(3'b001), .out(rt), .sel(immediate_rt));
  Multiplexer #(.width(2), .enable("false")) multiplexer_4 (
    .in0(Instruction[1:0]), .in1(Instruction[7:6]), .out(ALU_OP), .sel(Instruction[8]));
  not not_6 (not_6_out, Instruction[1]);
  and and_7 (and_7_out, and_2_out, not_6_out, not_7_out);
  not not_7 (not_7_out, Instruction[0]);
  not not_8 (not_8_out, Instruction[1]);
  and and_8 (and_8_out, and_2_out, not_8_out, Instruction[0]);
  and and_9 (immediate_rt, is_zero_2_out_2, xor_1_out);
  and and_10 (regwrite, is_zero_2_out_2, not_9_out);
  not not_9 (not_9_out, or_1_out);
  or or_1 (or_1_out, and_8_out, Instruction[8]);
  assign branch_value = {{2{Instruction[5]}}, Instruction[5:0]};  // Bit_Extender bit_extender_1
  or or_2 (branch_absolute, and_4_out, save_PC);
  or or_3 (memread, and_7_out, branch_relative);
  or or_4 (memwrite, or_1_out, save_PC);
  and and_11 (storeFromRegister, or_1_out, is_zero_2_out_2);

  assign rd = Instruction[5:3];
endmodule

module is_zero (
  input  [2:0] in_1,
  output out_2
);

  wire not_1_out, not_2_out, not_3_out;

  not not_1 (not_1_out, in_1[0]);
  not not_2 (not_2_out, in_1[1]);
  not not_3 (not_3_out, in_1[2]);
  and and_1 (out_2, not_1_out, not_2_out, not_3_out);
endmodule

module is_full (
  input  [2:0] in_1,
  output out_2
);

  and and_1 (out_2, in_1[0], in_1[1], in_1[2]);
endmodule

module is_zero_8 (
  input  [7:0] in_1,
  output out_2
);

  wire not_1_out, not_2_out, not_3_out, not_4_out, not_5_out, not_6_out, not_7_out, not_8_out;

  not not_1 (not_1_out, in_1[0]);
  not not_2 (not_2_out, in_1[1]);
  not not_3 (not_3_out, in_1[2]);
  not not_4 (not_4_out, in_1[3]);
  not not_5 (not_5_out, in_1[4]);
  not not_6 (not_6_out, in_1[5]);
  not not_7 (not_7_out, in_1[6]);
  not not_8 (not_8_out, in_1[7]);
  and and_1 (out_2, not_1_out, not_2_out, not_3_out, not_4_out, not_5_out, not_6_out, not_7_out, not_8_out);
endmodule
