// Logisim project sDatapath.circ as structural Verilog: 6 circuits, main circuit main
module main (
  input  reset
);

  wire Clock_out, is_zero_1_out_2;
  wire [1:0] control_1_alu_op;
  wire [7:0] alu_1_out_4, multiplexer_1_out, pc_1_instruction_address, registerfile_1_s;
  wire [10:0] rom_1_data;

  Clock Clock (.out(Clock_out));
  PC pc_1 (.C(Clock_out), .reset(reset), .instruction_address(pc_1_instruction_address));
  ROM #(.dataWidth(11)) rom_1 (.addr(pc_1_instruction_address), .data(rom_1_data));  // open: sel
  RegisterFile registerfile_1 (.Data(alu_1_out_4), .S(registerfile_1_s));  // open: rs, rt, rd, reset, C, T
  Control control_1 (
    .instruction(rom_1_data), .ALU_OP(control_1_alu_op));  // open: rs, rt, rd, immediate, immediate_value
  is_zero is_zero_1 (.in_1(control_1_alu_op), .out_2(is_zero_1_out_2));
  Multiplexer #(.width(8), .enable("false")) multiplexer_1 (
    .in0(registerfile_1_s), .out(multiplexer_1_out), .sel(is_zero_1_out_2));  // open: in1
  ALU alu_1 (.OP_code(control_1_alu_op), .A(multiplexer_1_out), .out_4(alu_1_out_4));  // open: B
endmodule

module PC (
  input  C,
  input  reset,
  output [7:0] instruction_address
);

  wire [7:0] adder_1_out;

  Adder adder_1 (.a(8'h1), .b(instruction_address), .out(adder_1_out));  // open: cin, cout
  Register #(.trigger("falling")) register_1 (
    .D(adder_1_out), .Q(instruction_address), .clk(C), .clr(reset));  // open: en
endmodule

module ALU (
  input  [1:0] OP_code,
  input  [7:0] A,
  input  [7:0] B,
  output [7:0] out_4
);

  wire [7:0] adder_1_out, and_1_out, subtractor_1_out;

  assign and_1_out = A & B;  // AND_Gate and_1, 8 bits wide
  Adder adder_1 (.a(A), .b(B), .out(adder_1_out));  // open: cin, cout
  Subtractor subtractor_1 (.a(A), .b(B), .out(subtractor_1_out));  // open: bin, bout
  Multiplexer #(.select(2), .width(8), .enable("false")) multiplexer_1 (
    .in0(B), .in1(and_1_out), .in2(adder_1_out), .in3(subtractor_1_out), .out(out_4), .sel(OP_code));
endmodule

module RegisterFile (
  input  [3:0] rs,
  input  [3:0] rt,
  input  [3:0] rd,
  input  [7:0] Data,
  input  reset,
  input  C,
  output [7:0] S,
  output [7:0] T
);

  wire decoder_1_out1, decoder_1_out2, decoder_1_out3, decoder_1_out4, decoder_1_out5, decoder_1_out6,
       decoder_1_out7, decoder_1_out8, decoder_1_out9, decoder_1_out10, decoder_1_out11, decoder_1_out12,
       decoder_1_out13, decoder_1_out14, decoder_1_out15;
  wire [7:0] register_1_q, register_2_q, register_3_q, register_4_q, register_5_q, register_6_q,
       register_7_q, register_8_q, register_9_q, register_10_q, register_11_q, register_12_q, register_13_q,
       register_14_q, register_15_q;

  Decoder #(.select(4), .enable("false")) decoder_1 (
    .out1(decoder_1_out1), .out2(decoder_1_out2), .out3(decoder_1_out3), .out4(decoder_1_out4),
    .out5(decoder_1_out5), .out6(decoder_1_out6), .out7(decoder_1_out7), .out8(decoder_1_out8),
    .out9(decoder_1_out9), .out10(decoder_1_out10), .out11(decoder_1_out11), .out12(decoder_1_out12),
    .out13(decoder_1_out13), .out14(decoder_1_out14), .out15(decoder_1_out15), .sel(rd));  // open: out0
  Register register_1 (.D(Data), .en(decoder_1_out1), .Q(register_1_q), .clk(C), .clr(reset));
  Register register_2 (.D(Data), .en(decoder_1_out2), .Q(register_2_q), .clk(C), .clr(reset));
  Register register_3 (.D(Data), .en(decoder_1_out3), .Q(register_3_q), .clk(C), .clr(reset));
  Register register_4 (.D(Data), .en(decoder_1_out4), .Q(register_4_q), .clk(C), .clr(reset));
  Register register_5 (.D(Data), .en(decoder_1_out5), .Q(register_5_q), .clk(C), .clr(reset));
  Register register_6 (.D(Data), .en(decoder_1_out6), .Q(register_6_q), .clk(C), .clr(reset));
  Register register_7 (.D(Data), .en(decoder_1_out7), .Q(register_7_q), .clk(C), .clr(reset));
  Register register_8 (.D(Data), .en(decoder_1_out8), .Q(register_8_q), .clk(C), .clr(reset));
  Register register_9 (.D(Data), .en(decoder_1_out9), .Q(register_9_q), .clk(C), .clr(reset));
  Register register_10 (.D(Data), .en(decoder_1_out10), .Q(register_10_q), .clk(C), .clr(reset));
  Register register_11 (.D(Data), .en(decoder_1_out11), .Q(register_11_q), .clk(C), .clr(reset));
  Register register_12 (.D(Data), .en(decoder_1_out12), .Q(register_12_q), .clk(C), .clr(reset));
  Register register_13 (.D(Data), .en(decoder_1_out13), .Q(register_13_q), .clk(C), .clr(reset));
  Register register_14 (.D(Data), .en(decoder_1_out14), .Q(register_14_q), .clk(C), .clr(reset));
  Register register_15 (.D(Data), .en(decoder_1_out15), .Q(register_15_q), .clk(C), .clr(reset));
  Multiplexer #(.select(4), .width(8), .enable("false")) multiplexer_1 (
    .in0({8{1'b0}}), .in1(register_1_q), .in2(register_2_q), .in3(register_3_q), .in4(register_4_q),
    .in5(register_5_q), .in6(register_6_q), .in7(register_7_q), .in8(register_8_q), .in9(register_9_q),
    .in10(register_10_q), .in11(register_11_q), .in12(register_12_q), .in13(register_13_q),
    .in14(register_14_q), .in15(register_15_q), .out(S), .sel(rs));
  Multiplexer #(.select(4), .width(8), .enable("false")) multiplexer_2 (
    .in0({8{1'b0}}), .in1(register_1_q), .in2(register_2_q), .in3(register_3_q), .in4(register_4_q),
    .in5(register_5_q), .in6(register_6_q), .in7(register_7_q), .in8(register_8_q), .in9(register_9_q),
    .in10(register_10_q), .in11(register_11_q), .in12(register_12_q), .in13(register_13_q),
    .in14(register_14_q), .in15(register_15_q), .out(T), .sel(rt));
endmodule

module Control (
  input  [10:0] instruction,
  output [3:0] rs,
  output [3:0] rt,
  output [3:0] rd,
  output [1:0] ALU_OP,
  output immediate,
  output [7:0] immediate_value
);

  wire decoder_1_out0;

  Decoder #(.select(3), .enable("false")) decoder_1 (
    .out0(decoder_1_out0), .sel(instruction[10:8]));  // open: out1, out2, out3, out4, out5, out6, out7
  Multiplexer #(.width(4), .enable("false")) multiplexer_1 (
    .in0(instruction[7:4]), .in1(4'b1111), .out(rs), .sel(instruction[10]));
  Multiplexer #(.width(4), .enable("false")) multiplexer_2 (
    .in0(4'b1111), .in1(instruction[7:4]), .out(rd), .sel(decoder_1_out0));

  assign ALU_OP = instruction[9:8];
  assign immediate = instruction[10];
  assign immediate_value = instruction[7:0];
  assign rt = instruction[3:0];
endmodule

module is_zero (
  input  [1:0] in_1,
  output out_2
);

  wire not_1_out, not_2_out;

  not not_1 (not_1_out, in_1[0]);
  not not_2 (not_2_out, in_1[1]);
  and and_1 (out_2, not_1_out, not_2_out);
endmodule
